// Logisim project Adder.circ as structural Verilog: 2 circuits, main circuit main
module main (
  input  in_1,
  input  in_2,
  input  in_3,
  input  in_4,
  input  in_5,
  input  in_6,
  input  in_7,
  input  in_8,
  output out_9,
  output out_10,
  output out_11,
  output out_12,
  output out_13,
  output out_14,
  output out_15
);

  wire n1_bit_adder_1_output_bit0, n1_bit_adder_1_output_bit1, n1_bit_adder_2_output_bit0,
       n1_bit_adder_2_output_bit1, n1_bit_adder_3_output_bit0, n1_bit_adder_3_output_bit1,
       n1_bit_adder_4_output_bit1, n1_bit_adder_5_output_bit0, n1_bit_adder_5_output_bit1,
       n1_bit_adder_6_output_bit1, n1_bit_adder_7_output_bit1, n1_bit_adder_8_output_bit1,
       n1_bit_adder_10_output_bit1;

  _1_bit_adder u_1_bit_adder_1 (
    .output_bit1(n1_bit_adder_1_output_bit1), .output_bit0(n1_bit_adder_1_output_bit0), .Input1(in_1),
    .Input2(in_5));
  _1_bit_adder u_1_bit_adder_2 (
    .output_bit1(n1_bit_adder_2_output_bit1), .output_bit0(n1_bit_adder_2_output_bit0), .Input1(in_2),
    .Input2(in_6));
  _1_bit_adder u_1_bit_adder_3 (
    .output_bit1(n1_bit_adder_3_output_bit1), .output_bit0(n1_bit_adder_3_output_bit0), .Input1(in_3),
    .Input2(in_7));
  _1_bit_adder u_1_bit_adder_4 (
    .output_bit1(n1_bit_adder_4_output_bit1), .output_bit0(out_15), .Input1(in_4), .Input2(in_8));
  _1_bit_adder u_1_bit_adder_5 (
    .output_bit1(n1_bit_adder_5_output_bit1), .output_bit0(n1_bit_adder_5_output_bit0),
    .Input1(n1_bit_adder_3_output_bit1), .Input2(n1_bit_adder_6_output_bit1));
  // Probe on n1_bit_adder_5_output_bit1
  _1_bit_adder u_1_bit_adder_6 (
    .output_bit1(n1_bit_adder_6_output_bit1), .output_bit0(out_14), .Input1(n1_bit_adder_3_output_bit0),
    .Input2(n1_bit_adder_4_output_bit1));
  _1_bit_adder u_1_bit_adder_7 (
    .output_bit1(n1_bit_adder_7_output_bit1), .output_bit0(out_12), .Input1(n1_bit_adder_2_output_bit1),
    .Input2(n1_bit_adder_8_output_bit1));
  _1_bit_adder u_1_bit_adder_8 (
    .output_bit1(n1_bit_adder_8_output_bit1), .output_bit0(out_13), .Input1(n1_bit_adder_2_output_bit0),
    .Input2(n1_bit_adder_5_output_bit0));
  _1_bit_adder u_1_bit_adder_9 (
    .output_bit1(out_9), .output_bit0(out_10), .Input1(n1_bit_adder_1_output_bit1),
    .Input2(n1_bit_adder_10_output_bit1));
  _1_bit_adder u_1_bit_adder_10 (
    .output_bit1(n1_bit_adder_10_output_bit1), .output_bit0(out_11), .Input1(n1_bit_adder_1_output_bit0),
    .Input2(n1_bit_adder_7_output_bit1));
endmodule

module _1_bit_adder (
  input  Input1,
  input  Input2,
  output output_bit1,
  output output_bit0
);

  and and_1 (output_bit1, Input2, Input1);
  xor xor_1 (output_bit0, Input1, Input2);
endmodule
