// Logisim project CPU.circ as structural Verilog: 5 circuits, main circuit main
module main (
);

  wire clock_1_out, undriven, undriven_2, undriven_3;
  wire [2:0] counter_1_q;

  Clock clock_1 (.out(clock_1_out));
  Counter #(.width(3), .max('h7)) counter_1 (
    .count(1'b1), .Q(counter_1_q), .clk(clock_1_out));  // open: load, D, carry, clr
  ROM rom_1 ();  // open: addr, data, sel
  Line_Decoder line_decoder_1 (
    .in_1(undriven), .in_2(undriven_2), .in_3(undriven_3));  // open: out_4, out_5, out_6, out_7, out_8, out_9, out_10, out_11
  RAM ram_1 ();  // open: addr, data, sel, clk, ld, clr
endmodule

module Adder (
  input  in_1,
  input  in_2,
  input  in_3,
  input  in_4,
  input  in_5,
  input  in_6,
  input  in_7,
  input  in_8,
  input  in_9,
  input  in_10,
  input  in_11,
  input  in_12,
  input  in_13,
  input  in_14,
  input  in_15,
  input  in_16,
  output out_17,
  output out_18,
  output out_19,
  output out_20,
  output out_21,
  output out_22,
  output out_23,
  output out_24
);

  wire and_1_out, and_2_out, and_3_out, and_4_out, and_5_out, and_6_out, and_7_out, xor_2_out, xor_4_out,
       xor_5_out, xor_6_out, xor_8_out, xor_10_out, xor_11_out;

  and and_1 (and_1_out, in_8, in_16);
  and and_2 (and_2_out, in_15, and_1_out);
  xor xor_1 (out_24, in_8, in_16);
  xor xor_2 (xor_2_out, in_15, and_1_out);
  and and_3 (and_3_out, in_7, xor_2_out);
  xor xor_3 (out_23, in_7, xor_2_out);
  and and_4 (and_4_out, and_2_out, and_3_out);
  xor xor_4 (xor_4_out, and_3_out, and_2_out);
  and and_5 (and_5_out, xor_4_out, in_14);
  xor xor_5 (xor_5_out, xor_4_out, in_14);
  xor xor_6 (xor_6_out, and_4_out, and_5_out);
  xor xor_7 (out_22, in_6, xor_5_out);
  and and_6 (and_6_out, in_13, xor_6_out);
  xor xor_8 (xor_8_out, in_13, xor_6_out);
  and and_7 (and_7_out, in_5, xor_8_out);
  xor xor_9 (out_18, in_5, xor_8_out);
  xor xor_10 (xor_10_out, and_7_out, and_6_out);
  // AND_Gate and_8 has open pins: in1=xor_10_out, in3=in_12, out=open
  xor xor_11 (xor_11_out, in_12, xor_10_out);
  // XOR_Gate xor_12 has open pins: in1=xor_11_out, in3=in_4, out=open
endmodule

module Half_Adder (
  input  B2,
  input  B1,
  output C_out,
  output O1
);

  wire and_1_out, and_2_out, not_1_out, not_2_out;

  not not_1 (not_1_out, B2);
  not not_2 (not_2_out, B1);
  and and_1 (and_1_out, not_1_out, B1);
  and and_2 (and_2_out, not_2_out, B2);
  and and_3 (C_out, B2, B1);
  or or_1 (O1, and_1_out, and_2_out);
endmodule

module Full_Adder (
  input  C_in,
  input  B1,
  input  B2,
  output C_out,
  output O2,
  output O1
);

  wire half_adder_1_c_out;

  Half_Adder half_adder_1 (.B2(B1), .B1(B2), .C_out(half_adder_1_c_out), .O1(O1));
  Half_Adder half_adder_2 (.B2(C_in), .B1(half_adder_1_c_out), .C_out(C_out), .O1(O2));
endmodule

module Line_Decoder (
  input  in_1,
  input  in_2,
  input  in_3,
  output out_4,
  output out_5,
  output out_6,
  output out_7,
  output out_8,
  output out_9,
  output out_10,
  output out_11
);

  wire not_1_out, not_2_out, not_3_out, not_4_out, not_5_out, not_6_out, not_7_out, not_8_out, not_9_out,
       not_10_out, not_11_out, not_12_out;

  not not_1 (not_1_out, in_3);
  not not_2 (not_2_out, in_2);
  not not_3 (not_3_out, in_2);
  not not_4 (not_4_out, in_3);
  not not_5 (not_5_out, in_1);
  not not_6 (not_6_out, in_1);
  not not_7 (not_7_out, in_3);
  not not_8 (not_8_out, in_1);
  not not_9 (not_9_out, in_2);
  not not_10 (not_10_out, in_1);
  not not_11 (not_11_out, in_2);
  and and_1 (out_4, in_1, in_2, in_3);
  and and_2 (out_5, in_1, in_2, not_1_out);
  and and_3 (out_6, in_1, not_2_out, in_3);
  and and_4 (out_7, in_1, not_3_out, not_4_out);
  and and_5 (out_8, not_5_out, in_2, in_3);
  and and_6 (out_9, not_6_out, in_2, not_7_out);
  and and_7 (out_10, not_8_out, not_9_out, in_3);
  and and_8 (out_11, not_10_out, not_11_out, not_12_out);
  not not_12 (not_12_out, in_3);
endmodule
